// Logisim project counter project.circ as structural Verilog: 1 circuit, main circuit main
module main (
  output out_1,
  output out_2,
  output out_3,
  output out_4,
  output out_5
);

  wire and_1_out, and_2_out, and_3_out, and_4_out, and_5_out, and_6_out, and_7_out, and_8_out, and_9_out,
       and_10_out, and_11_out, clock_1_out, not_1_out, not_2_out, not_3_out, not_4_out, not_5_out, not_6_out,
       not_7_out, or_1_out, or_2_out, or_3_out, or_4_out;

  not not_1 (not_1_out, out_3);
  not not_2 (not_2_out, out_1);
  not not_3 (not_3_out, out_4);
  not not_4 (not_4_out, out_3);
  not not_5 (not_5_out, out_2);
  not not_6 (not_6_out, out_3);
  not not_7 (not_7_out, out_4);
  and and_1 (and_1_out, out_5, out_4, not_1_out);
  or or_1 (or_1_out, not_1_out, out_4);
  and and_2 (and_2_out, out_3, not_3_out);
  and and_3 (and_3_out, not_4_out, out_1, not_5_out, out_4);
  and and_4 (and_4_out, not_6_out, out_5);
  and and_5 (and_5_out, and_1_out, not_2_out);
  and and_6 (and_6_out, out_2, and_1_out);
  or or_2 (or_2_out, and_2_out, and_3_out);
  and and_7 (and_7_out, not_5_out, out_1);
  or or_3 (or_3_out, and_6_out, out_1);
  and and_8 (and_8_out, and_7_out, and_4_out);
  and and_9 (and_9_out, and_7_out, out_5);
  and and_10 (and_10_out, out_3, out_5);
  and and_11 (and_11_out, out_5, not_7_out);
  or or_4 (or_4_out, and_9_out, and_11_out);
  Clock clock_1 (.out(clock_1_out));
  J_K_Flip_Flop j_k_ff_1 (.J(and_5_out), .clk(clock_1_out), .K(1'b1), .Q(out_2));  // open: Qn, preset, en, reset
  J_K_Flip_Flop j_k_ff_2 (.J(or_3_out), .clk(clock_1_out), .K(1'b1), .Q(out_1));  // open: Qn, preset, en, reset
  J_K_Flip_Flop j_k_ff_3 (.J(or_1_out), .clk(clock_1_out), .K(or_2_out), .Q(out_5));  // open: Qn, preset, en, reset
  J_K_Flip_Flop j_k_ff_4 (.J(and_10_out), .clk(clock_1_out), .K(and_8_out), .Q(out_4));  // open: Qn, preset, en, reset
  J_K_Flip_Flop j_k_ff_5 (.J(or_4_out), .clk(clock_1_out), .K(1'b1), .Q(out_3));  // open: Qn, preset, en, reset

  // Notes on the sheet:
  //   X0
  //   X1
  //   A0
  //   A1
  //   A2
  //   sayim sonucu ==>
endmodule
